# Fritzing sketch Mini-project (saved by Fritzing 0.9.3b)
breadboards: 1

parts:
  Part1 = Adafruit Metro Mini [part_number="Adafruit #2590"]
  M1 = Dagu DGServo 9g (Pan and tilt) [part_number=RS001B]
  M2 = Dagu DGServo 9g (Pan and tilt) [part_number=RS001B]
  M3 = Dagu DGServo 9g (Pan and tilt) [part_number=RS001B]
  M4 = Dagu DGServo 9g (Pan and tilt) [part_number=RS001B]
  LCD1 = LCD screen
  R1 = Resistor [tolerance=±5% resistance=220 package="2512 [SMD]"]
  J1 = Piezo Speaker

nets:
  N1: Part1.IO13, J1.pin2
  N2: Part1.IO11, LCD1.RS
  N3: Part1.IO10, LCD1.R/W
  N4: Part1.IO9, LCD1.DB0
  N5: Part1.IO8, LCD1.DB4
  N6: Part1.IO7, LCD1.DB5
  N7: Part1.IO6, LCD1.DB6
  N8: Part1.IO5, LCD1.DB7
  N9: Part1.IO4, M3.pulse
  N10: Part1.IO3, M4.pulse
  N11: Part1.IO2, M2.pulse
  N12: Part1.IO1, M1.pulse
  VCC: Part1.+5V, M1.vcc, M2.vcc, LCD1.VDD
  GND: Part1.GND, M1.gnd, M2.gnd, LCD1.VSS, LCD1.E, LCD1.LED-, R1.Pin_0, J1.pin1
  N13: LCD1.LED+, R1.Pin_1

custom parts:
  Adafruit Metro Mini: We sure love the ATmega328 here at Adafruit, and we use them a lot for our own projects. The processor has plenty of GPIO, Analog inputs, hardware UART SPI and I2C, timers and PWM galore - just enough for most simple projects. When we need to go small, we use a Pro Trinket 3V or 5V, but if you want to have USB-to-Serial built in, we reach for an Adafruit METRO Mini. METRO Mini is the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
